# Fritzing sketch Flowers (saved by Fritzing 0.9.3b)
breadboards: 1

parts:
  Part1 = Arduino Uno (Rev3) - ICSP
  DS1 = DS18B20 1-Wire Temperature Sensor [part_number=DS18B20]
  R1 = Resistor [tolerance=±5% resistance=4.7k package=THT]

nets:
  N1: Part1.D2, DS1.DQ, R1.Pin_0
  5V: Part1.5V, DS1.VDD, R1.Pin_1
  GND: Part1.GND, DS1.GND

notes:
  ->Zielony - A0 na czujniku wilgotnosci gleby
  ->Żółty - A0 na drugim czujniku wilgotnosci gleby
  ->Czarny - Uziemienie
  ->Czerwony - 5V
